// Logisim project 16BitCarryLookaheadAddition.circ as structural Verilog: 11 circuits, main circuit 16BitAdder
module _16BitAdder (
  input  C,
  input  A0,
  input  B0,
  input  A1,
  input  B1,
  input  A2,
  input  B2,
  input  A3,
  input  B3,
  input  A4,
  input  B4,
  input  A5,
  input  B5,
  input  A6,
  input  B6,
  input  A7,
  input  B7,
  input  A8,
  input  B8,
  input  A9,
  input  B9,
  input  A10,
  input  B10,
  input  A11,
  input  B11,
  input  A12,
  input  B12,
  input  A13,
  input  B13,
  input  A14,
  input  B14,
  input  A15,
  input  B15,
  output S0,
  output S1,
  output S2,
  output S3,
  output S4,
  output S5,
  output S6,
  output S7,
  output S8,
  output S9,
  output S10,
  output S11,
  output S12,
  output S13,
  output S14,
  output S15,
  output C_2
);

  wire and_1_out, and_2_out, and_3_out, and_4_out, and_5_out, and_6_out, and_7_out, and_8_out, and_9_out,
       and_10_out, and_11_out, and_12_out, and_13_out, and_14_out, and_15_out, and_16_out, and_17_out,
       and_18_out, and_19_out, and_20_out, and_21_out, and_22_out, and_23_out, and_24_out, and_25_out,
       and_26_out, and_27_out, and_28_out, C1_out, C2_out, C3_out, C4_out, C5_out, C6_out, C7_out, C8_c8,
       C9_c8, C10_c8, C11_c8, C12_c8, C13_c8, C14_c8, C15_c15, G0_out, G1_out, G2_out, G3_out, G4_out,
       G5_out, G6_out, G7_out, G8_out, G9_out, G10_out, G11_out, G12_out, G13_out, G14_out, G15_out, P0_out,
       P1_out, P2_out, P3_out, P4_out, P5_out, P6_out, P7_out, P8_out, P9_out, P10_out, P11_out, P12_out,
       P13_out, P14_out, P15_out;

  and G0 (G0_out, A0, B0);
  xor P0 (P0_out, A0, B0);
  and G1 (G1_out, A1, B1);
  xor P1 (P1_out, A1, B1);
  and G2 (G2_out, A2, B2);
  xor P2 (P2_out, A2, B2);
  and G3 (G3_out, A3, B3);
  xor P3 (P3_out, A3, B3);
  and G4 (G4_out, A4, B4);
  xor P4 (P4_out, A4, B4);
  and G5 (G5_out, A5, B5);
  xor P5 (P5_out, A5, B5);
  and G6 (G6_out, A6, B6);
  xor P6 (P6_out, A6, B6);
  and G7 (G7_out, A7, B7);
  xor P7 (P7_out, A7, B7);
  and G8 (G8_out, A8, B8);
  xor P8 (P8_out, A8, B8);
  and G9 (G9_out, A9, B9);
  xor P9 (P9_out, A9, B9);
  and G10 (G10_out, A10, B10);
  xor P10 (P10_out, A10, B10);
  and G11 (G11_out, A11, B11);
  xor P11 (P11_out, A11, B11);
  and G12 (G12_out, A12, B12);
  xor P12 (P12_out, A12, B12);
  and G13 (G13_out, A13, B13);
  xor P13 (P13_out, A13, B13);
  and G14 (G14_out, A14, B14);
  xor P14 (P14_out, A14, B14);
  and G15 (G15_out, A15, B15);
  xor P15 (P15_out, A15, B15);
  and and_1 (and_1_out, C, P0_out);
  and and_2 (and_2_out, C, P0_out, P1_out);
  and and_3 (and_3_out, G0_out, P1_out);
  and and_4 (and_4_out, C, P0_out, P1_out, P2_out);
  and and_5 (and_5_out, G0_out, P1_out, P2_out);
  and and_6 (and_6_out, G1_out, P2_out);
  or C1 (C1_out, G0_out, and_1_out);
  or C2 (C2_out, and_2_out, G1_out, and_3_out);
  or C3 (C3_out, and_4_out, and_5_out, and_6_out, G2_out);
  and and_7 (and_7_out, C, P1_out, P2_out, P3_out, P0_out);
  and and_8 (and_8_out, G0_out, P1_out, P2_out, P3_out);
  or C4 (C4_out, and_7_out, and_8_out, G3_out, and_9_out, and_10_out);
  and and_9 (and_9_out, G1_out, P2_out, P3_out);
  and and_10 (and_10_out, G2_out, P3_out);
  and and_11 (and_11_out, C, P0_out, P1_out, P2_out, P3_out, P4_out);
  and and_12 (and_12_out, G0_out, P1_out, P2_out, P3_out, P4_out);
  or C5 (C5_out, and_11_out, and_12_out, G4_out, and_13_out, and_14_out, and_15_out);
  and and_13 (and_13_out, G1_out, P2_out, P3_out, P4_out);
  and and_14 (and_14_out, G2_out, P3_out, P4_out);
  and and_15 (and_15_out, G3_out, P4_out);
  and and_16 (and_16_out, G0_out, P1_out, P2_out, P3_out, P4_out, P5_out);
  and and_17 (and_17_out, G1_out, P2_out, P3_out, P4_out, P5_out);
  and and_18 (and_18_out, G2_out, P3_out, G4_out, P5_out);
  and and_19 (and_19_out, G3_out, P4_out, P5_out);
  and and_20 (and_20_out, G4_out, P5_out);
  and and_21 (and_21_out, C, P0_out, P1_out, P2_out, P3_out, P4_out, P5_out, P6_out);
  and and_22 (and_22_out, G0_out, P1_out, P2_out, P3_out, P4_out, P5_out, P6_out);
  and and_23 (and_23_out, G1_out, P2_out, P3_out, P4_out, P5_out, P6_out);
  and and_24 (and_24_out, G2_out, P3_out, P4_out, P5_out, P6_out);
  and and_25 (and_25_out, G3_out, P4_out, P5_out, P6_out);
  and and_26 (and_26_out, G4_out, P5_out, P6_out);
  and and_27 (and_27_out, G5_out, P6_out);
  and and_28 (and_28_out, C, P0_out, P1_out, P2_out, P3_out, P5_out, P4_out);
  or C6 (C6_out, and_28_out, and_16_out, and_17_out, G5_out, and_18_out, and_19_out, and_20_out);
  or C7 (C7_out, G6_out, and_21_out, and_22_out, and_23_out, and_24_out, and_25_out, and_26_out, and_27_out);
  Carry8 C8 (
    .C(C), .P0(P0_out), .P1(P1_out), .P2(P2_out), .P3(P3_out), .P4(P4_out), .P5(P5_out), .P6(P6_out),
    .P7(P7_out), .G0(G0_out), .G1(G1_out), .G2(G2_out), .G3(G3_out), .G4(G4_out), .G5(G5_out), .G6(G6_out),
    .G7(G7_out), .C8(C8_c8));
  Carry9 C9 (
    .C(C), .P0(P0_out), .P1(P1_out), .P2(P2_out), .P3(P3_out), .P4(P4_out), .P5(P5_out), .P6(P6_out),
    .P7(P7_out), .P8(P8_out), .G0(G0_out), .G1(G1_out), .G2(G2_out), .G3(G3_out), .G4(G4_out), .G5(G5_out),
    .G6(G6_out), .G7(G7_out), .G8(G8_out), .C8(C9_c8));
  Carry10 C10 (
    .C(C), .P0(P0_out), .P1(P1_out), .P2(P2_out), .P3(P3_out), .P4(P4_out), .P5(P5_out), .P6(P6_out),
    .P7(P7_out), .P8(P8_out), .P9(P9_out), .G0(G0_out), .G1(G1_out), .G2(G2_out), .G3(G3_out), .G4(G4_out),
    .G5(G5_out), .G6(G6_out), .G7(G7_out), .G8(G8_out), .G9(G9_out), .C8(C10_c8));
  Carry11 C11 (
    .C(C), .P0(P0_out), .P1(P1_out), .P2(P2_out), .P3(P3_out), .P4(P4_out), .P5(P5_out), .P6(P6_out),
    .P7(P7_out), .P8(P8_out), .P9(P9_out), .P10(P10_out), .G0(G0_out), .G1(G1_out), .G2(G2_out), .G3(G3_out),
    .G4(G4_out), .G5(G5_out), .G6(G6_out), .G7(G7_out), .G8(G8_out), .G9(G9_out), .G10(G10_out), .C8(C11_c8));
  Carry12 C12 (
    .C(C), .P0(P0_out), .P1(P1_out), .P2(P2_out), .P3(P3_out), .P4(P4_out), .P5(P5_out), .P6(P6_out),
    .P7(P7_out), .P8(P8_out), .P9(P9_out), .P10(P10_out), .P11(P11_out), .G0(G0_out), .G1(G1_out),
    .G2(G2_out), .G3(G3_out), .G4(G4_out), .G5(G5_out), .G6(G6_out), .G7(G7_out), .G8(G8_out), .G9(G9_out),
    .G10(G10_out), .G11(G11_out), .C8(C12_c8));
  Carry13 C13 (
    .C(C), .P0(P0_out), .P1(P1_out), .P2(P2_out), .P3(P3_out), .P4(P4_out), .P5(P5_out), .P6(P6_out),
    .P7(P7_out), .P8(P8_out), .P9(P9_out), .P10(P10_out), .P11(P11_out), .P12(P12_out), .G0(G0_out),
    .G1(G1_out), .G2(G2_out), .G3(G3_out), .G4(G4_out), .G5(G5_out), .G6(G6_out), .G7(G7_out), .G8(G8_out),
    .G9(G9_out), .G10(G10_out), .G11(G11_out), .G12(G12_out), .C8(C13_c8));
  Carry14 C14 (
    .C(C), .P0(P0_out), .P1(P1_out), .P2(P2_out), .P3(P3_out), .P4(P4_out), .P5(P5_out), .P6(P6_out),
    .P7(P7_out), .P8(P8_out), .P9(P9_out), .P10(P10_out), .P11(P11_out), .P12(P12_out), .P13(P13_out),
    .G0(G0_out), .G1(G1_out), .G2(G2_out), .G3(G3_out), .G4(G4_out), .G5(G5_out), .G6(G6_out), .G7(G7_out),
    .G8(G8_out), .G9(G9_out), .G10(G10_out), .G11(G11_out), .G12(G12_out), .G13(G13_out), .C8(C14_c8));
  Carry15 C15 (
    .C(C), .P0(P0_out), .P1(P1_out), .P2(P2_out), .P3(P3_out), .P4(P4_out), .P5(P5_out), .P6(P6_out),
    .P7(P7_out), .P8(P8_out), .P9(P9_out), .P10(P10_out), .P11(P11_out), .P12(P12_out), .P13(P13_out),
    .P14(P14_out), .G0(G0_out), .G1(G1_out), .G2(G2_out), .G3(G3_out), .G4(G4_out), .G5(G5_out), .G6(G6_out),
    .G7(G7_out), .G8(G8_out), .G9(G9_out), .G10(G10_out), .G11(G11_out), .G12(G12_out), .G13(G13_out),
    .G14(G14_out), .C15(C15_c15));
  Carry16 C16 (
    .C(C), .P0(P0_out), .P1(P1_out), .P2(P2_out), .P3(P3_out), .P4(P4_out), .P5(P5_out), .P6(P6_out),
    .P7(P7_out), .P8(P8_out), .P9(P9_out), .P10(P10_out), .P11(P11_out), .P12(P12_out), .P13(P13_out),
    .P14(P14_out), .P15(P15_out), .G0(G0_out), .G1(G1_out), .G2(G2_out), .G3(G3_out), .G4(G4_out),
    .G5(G5_out), .G6(G6_out), .G7(G7_out), .G8(G8_out), .G9(G9_out), .G10(G10_out), .G11(G11_out),
    .G12(G12_out), .G13(G13_out), .G14(G14_out), .G15(G15_out), .C15(C_2));
  xor xor_1 (S0, C, P0_out);
  xor xor_2 (S1, C1_out, P1_out);
  xor xor_3 (S2, C2_out, P2_out);
  xor xor_4 (S3, C3_out, P3_out);
  xor xor_5 (S4, C4_out, P4_out);
  xor xor_6 (S5, C5_out, P5_out);
  xor xor_7 (S6, C6_out, P6_out);
  xor xor_8 (S7, C7_out, P7_out);
  xor xor_9 (S8, C8_c8, P8_out);
  xor xor_10 (S9, C9_c8, P9_out);
  xor xor_11 (S10, C10_c8, P10_out);
  xor xor_12 (S11, C11_c8, P11_out);
  xor xor_13 (S12, C12_c8, P12_out);
  xor xor_14 (S13, C13_c8, P13_out);
  xor xor_15 (S14, C14_c8, P14_out);
  xor xor_16 (S15, C15_c15, P15_out);
endmodule

module Carry8 (
  input  C,
  input  P0,
  input  P1,
  input  P2,
  input  P3,
  input  P4,
  input  P5,
  input  P6,
  input  P7,
  input  G0,
  input  G1,
  input  G2,
  input  G3,
  input  G4,
  input  G5,
  input  G6,
  input  G7,
  output C8
);

  wire and_1_out, and_2_out, and_3_out, and_4_out, and_5_out, and_6_out, and_7_out, and_8_out;

  and and_1 (and_1_out, C, P0, P1, P2, P3, P4, P5, P6, P7);
  and and_2 (and_2_out, G0, P1, P2, P3, P4, P5, P6, P7);
  and and_3 (and_3_out, G1, P2, P3, P4, P5, P6, P7);
  and and_4 (and_4_out, G2, P3, P4, P5, P6, P7);
  and and_5 (and_5_out, G3, P4, P5, P6, P7);
  and and_6 (and_6_out, G4, P5, P6, P7);
  and and_7 (and_7_out, G5, P6, P7);
  and and_8 (and_8_out, G6, P7);
  or or_1 (C8, and_1_out, and_2_out, and_3_out, and_4_out, and_5_out, and_6_out, and_7_out, and_8_out, G7);
endmodule

module Carry9 (
  input  C,
  input  P0,
  input  P1,
  input  P2,
  input  P3,
  input  P4,
  input  P5,
  input  P6,
  input  P7,
  input  P8,
  input  G0,
  input  G1,
  input  G2,
  input  G3,
  input  G4,
  input  G5,
  input  G6,
  input  G7,
  input  G8,
  output C8
);

  wire and_1_out, and_2_out, and_3_out, and_4_out, and_5_out, and_6_out, and_7_out, and_8_out, and_9_out;

  and and_1 (and_1_out, G6, P7, P8);
  and and_2 (and_2_out, G7, P8);
  and and_3 (and_3_out, G0, P1, P2, P3, P4, P5, P6, P7, P8);
  and and_4 (and_4_out, G1, P2, P3, P4, P5, P6, P7, P8);
  and and_5 (and_5_out, G2, P3, P4, P5, P6, P7, P8);
  and and_6 (and_6_out, G3, P4, P5, P6, P7, P7);
  and and_7 (and_7_out, G4, P5, P6, P7, P8);
  and and_8 (and_8_out, G5, P6, P7, P8);
  and and_9 (and_9_out, C, P0, P1, P2, P3, P4, P5, P6, P7, P8);
  or or_1 (C8, and_9_out, and_3_out, and_4_out, and_5_out, and_6_out, and_7_out, and_8_out, and_1_out, and_2_out, G8);
endmodule

module Carry10 (
  input  C,
  input  P0,
  input  P1,
  input  P2,
  input  P3,
  input  P4,
  input  P5,
  input  P6,
  input  P7,
  input  P8,
  input  P9,
  input  G0,
  input  G1,
  input  G2,
  input  G3,
  input  G4,
  input  G5,
  input  G6,
  input  G7,
  input  G8,
  input  G9,
  output C8
);

  wire and_1_out, and_2_out, and_3_out, and_4_out, and_5_out, and_6_out, and_7_out, and_8_out, and_9_out,
       and_10_out;

  and and_1 (and_1_out, G8, P9);
  and and_2 (and_2_out, G0, P1, P2, P3, P4, P5, P6, P7, P8, P9);
  and and_3 (and_3_out, G1, P2, P3, P4, P5, P6, P7, P8, P9);
  and and_4 (and_4_out, G2, P3, P4, P5, P6, P7, P8, P9);
  and and_5 (and_5_out, G3, P4, P5, P6, P7, P8, P9);
  and and_6 (and_6_out, G4, P5, P6, P7, P8, P9);
  and and_7 (and_7_out, G5, P6, P7, P8, P9);
  and and_8 (and_8_out, G6, P7, P8, P8);
  and and_9 (and_9_out, G7, P8, P9);
  and and_10 (and_10_out, C, P0, P1, P2, P3, P5, P6, P7, P8, P9);
  or or_1 (C8, and_10_out, and_2_out, and_3_out, and_4_out, and_5_out, and_6_out, and_7_out, and_8_out, and_9_out, and_1_out, G9);
endmodule

module Carry11 (
  input  C,
  input  P0,
  input  P1,
  input  P2,
  input  P3,
  input  P4,
  input  P5,
  input  P6,
  input  P7,
  input  P8,
  input  P9,
  input  P10,
  input  G0,
  input  G1,
  input  G2,
  input  G3,
  input  G4,
  input  G5,
  input  G6,
  input  G7,
  input  G8,
  input  G9,
  input  G10,
  output C8
);

  wire and_1_out, and_2_out, and_3_out, and_4_out, and_5_out, and_6_out, and_7_out, and_8_out, and_9_out,
       and_10_out, and_11_out;

  and and_1 (and_1_out, G7, P8, P9, P10);
  and and_2 (and_2_out, G8, P9, P10);
  and and_3 (and_3_out, G9, P10);
  and and_4 (and_4_out, G0, P1, P2, P3, P4, P5, P6, P7, P8, P9, P10);
  and and_5 (and_5_out, G1, P2, P3, P4, P5, P6, P7, P8, P9, P10);
  and and_6 (and_6_out, G2, P3, P4, P5, P6, P7, P8, P9, P10);
  and and_7 (and_7_out, G3, P4, P5, P6, P7, P8, P9, P10);
  and and_8 (and_8_out, G4, P5, P6, P7, P8, P9, P10);
  and and_9 (and_9_out, G5, P6, P7, P8, P9, P10);
  and and_10 (and_10_out, G6, P7, P8, P9, P10);
  and and_11 (and_11_out, C, P0, P1, P2, P3, P4, P5, P6, P7, P8, P9, P10);
  or or_1 (C8, and_11_out, and_4_out, and_5_out, and_6_out, and_7_out, and_8_out, and_9_out, and_10_out, and_1_out, and_2_out, and_3_out, G10);
endmodule

module Carry12 (
  input  C,
  input  P0,
  input  P1,
  input  P2,
  input  P3,
  input  P4,
  input  P5,
  input  P6,
  input  P7,
  input  P8,
  input  P9,
  input  P10,
  input  P11,
  input  G0,
  input  G1,
  input  G2,
  input  G3,
  input  G4,
  input  G5,
  input  G6,
  input  G7,
  input  G8,
  input  G9,
  input  G10,
  input  G11,
  output C8
);

  wire and_1_out, and_2_out, and_3_out, and_4_out, and_5_out, and_6_out, and_7_out, and_8_out, and_9_out,
       and_10_out, and_11_out, and_12_out;

  and and_1 (and_1_out, G0, P1, P2, P3, P4, P5, P6, P7, P8, P9, P10, P11);
  and and_2 (and_2_out, G1, P2, P3, P4, P5, P6, P7, P8, P9, P10, P11);
  and and_3 (and_3_out, G2, P3, P4, P5, P6, P7, P8, P9, P10, P11);
  and and_4 (and_4_out, G3, P4, P5, P6, P7, P8, P9, P10, P11);
  and and_5 (and_5_out, G4, P5, P6, P7, P8, P9, P10, P11);
  and and_6 (and_6_out, G5, P6, P7, P8, P9, P10, P11);
  and and_7 (and_7_out, G6, P7, P8, P9, P10, P11);
  and and_8 (and_8_out, G7, P8, P9, P10, P11);
  and and_9 (and_9_out, G8, P9, P10, P11);
  and and_10 (and_10_out, G9, P10, P11);
  and and_11 (and_11_out, G10, P11);
  and and_12 (and_12_out, C, P0, P1, P2, P3, P4, P5, P6, P7, P8, P9, P10, P11);
  or or_1 (C8, and_12_out, and_1_out, and_2_out, and_3_out, and_4_out, and_5_out, and_6_out, and_7_out, and_8_out, and_9_out, and_10_out, and_11_out, G11);
endmodule

module Carry13 (
  input  C,
  input  P0,
  input  P1,
  input  P2,
  input  P3,
  input  P4,
  input  P5,
  input  P6,
  input  P7,
  input  P8,
  input  P9,
  input  P10,
  input  P11,
  input  P12,
  input  G0,
  input  G1,
  input  G2,
  input  G3,
  input  G4,
  input  G5,
  input  G6,
  input  G7,
  input  G8,
  input  G9,
  input  G10,
  input  G11,
  input  G12,
  output C8
);

  wire and_1_out, and_2_out, and_3_out, and_4_out, and_5_out, and_6_out, and_7_out, and_8_out, and_9_out,
       and_10_out, and_11_out, and_12_out, and_13_out;

  and and_1 (and_1_out, G0, P1, P2, P3, P4, P5, P6, P7, P8, P9, P10, P11, P12);
  and and_2 (and_2_out, G1, P2, P3, P4, P5, P6, P7, P8, P9, P10, P11, P12);
  and and_3 (and_3_out, G2, P3, P4, P5, P6, P7, P8, P9, P10, P11, P12);
  and and_4 (and_4_out, G3, P4, P5, P6, P7, P8, P9, P10, P11, P12);
  and and_5 (and_5_out, G4, P5, P6, P7, P8, P9, P10, P11, P12);
  and and_6 (and_6_out, G5, P6, P7, P8, P9, P10, P11, P12);
  and and_7 (and_7_out, G6, P7, P8, P9, P10, P11, P12);
  and and_8 (and_8_out, G7, P8, P9, P10, P11, P12);
  and and_9 (and_9_out, G8, P9, P10, P11, P12);
  and and_10 (and_10_out, G9, P10, P11, P12);
  and and_11 (and_11_out, G10, P11, P12);
  and and_12 (and_12_out, G11, P12);
  and and_13 (and_13_out, C, P0, P1, P2, P3, P4, P5, P6, P7, P8, P9, P10, P11, P12);
  or or_1 (C8, and_13_out, and_1_out, and_2_out, and_3_out, and_4_out, and_5_out, and_6_out, and_7_out, and_8_out, and_9_out, and_10_out, and_11_out, and_12_out, G12);
endmodule

module Carry14 (
  input  C,
  input  P0,
  input  P1,
  input  P2,
  input  P3,
  input  P4,
  input  P5,
  input  P6,
  input  P7,
  input  P8,
  input  P9,
  input  P10,
  input  P11,
  input  P12,
  input  P13,
  input  G0,
  input  G1,
  input  G2,
  input  G3,
  input  G4,
  input  G5,
  input  G6,
  input  G7,
  input  G8,
  input  G9,
  input  G10,
  input  G11,
  input  G12,
  input  G13,
  output C8
);

  wire and_1_out, and_2_out, and_3_out, and_4_out, and_5_out, and_6_out, and_7_out, and_8_out, and_9_out,
       and_10_out, and_11_out, and_12_out, and_13_out, and_14_out;

  and and_1 (and_1_out, G0, P1, P2, P3, P4, P5, P6, P7, P8, P9, P10, P11, P12, P13);
  and and_2 (and_2_out, G1, P2, P3, P4, P5, P6, P7, P8, P9, P10, P11, P12, P13);
  and and_3 (and_3_out, G2, P3, P4, P5, P6, P7, P8, P9, P10, P11, P12, P13);
  and and_4 (and_4_out, G3, P4, P5, P6, P7, P8, P9, P10, P11, P12, P13);
  and and_5 (and_5_out, G4, P5, P6, P7, P8, P9, P10, P11, P12, P13);
  and and_6 (and_6_out, G5, P6, P7, P8, P9, P10, P11, P12, P13);
  and and_7 (and_7_out, G6, P7, P8, P9, P10, P11, P12, P13);
  and and_8 (and_8_out, G7, P8, P9, P10, P11, P12, P13);
  and and_9 (and_9_out, G8, P9, P10, P11, P12, P13);
  and and_10 (and_10_out, G9, P10, P11, P12, P13);
  and and_11 (and_11_out, G10, P11, P12, P13);
  and and_12 (and_12_out, G11, P12, P13);
  and and_13 (and_13_out, G12, P13);
  and and_14 (and_14_out, C, P0, P1, P2, P3, P4, P5, P6, P7, P8, P9, P10, P11, P12, P13);
  or or_1 (C8, and_14_out, and_1_out, and_2_out, and_3_out, and_4_out, and_5_out, and_6_out, and_7_out, and_8_out, and_9_out, and_10_out, and_11_out, and_12_out, and_13_out, G13);
endmodule

module Carry15 (
  input  C,
  input  P0,
  input  P1,
  input  P2,
  input  P3,
  input  P4,
  input  P5,
  input  P6,
  input  P7,
  input  P8,
  input  P9,
  input  P10,
  input  P11,
  input  P12,
  input  P13,
  input  P14,
  input  G0,
  input  G1,
  input  G2,
  input  G3,
  input  G4,
  input  G5,
  input  G6,
  input  G7,
  input  G8,
  input  G9,
  input  G10,
  input  G11,
  input  G12,
  input  G13,
  input  G14,
  output C15
);

  wire and_1_out, and_2_out, and_3_out, and_4_out, and_5_out, and_6_out, and_7_out, and_8_out, and_9_out,
       and_10_out, and_11_out, and_12_out, and_13_out, and_14_out, and_15_out;

  and and_1 (and_1_out, G0, P1, P2, P3, P4, P5, P6, P7, P8, P9, P10, P11, P12, P13, P14);
  and and_2 (and_2_out, G1, P2, P3, P4, P5, P6, P7, P8, P9, P10, P11, P12, P13, P14);
  and and_3 (and_3_out, G2, P3, P4, P5, P6, P7, P8, P9, P10, P11, P12, P13, P14);
  and and_4 (and_4_out, G3, P4, P5, P6, P7, P8, P9, P10, P11, P12, P13, P14);
  and and_5 (and_5_out, G4, P5, P6, P7, P8, P9, P10, P11, P12, P13, P14);
  and and_6 (and_6_out, G5, P6, P7, P8, P9, P10, P11, P12, P13, P14);
  and and_7 (and_7_out, G6, P7, P8, P9, P10, P11, P12, P13, P14);
  and and_8 (and_8_out, G7, P8, P9, P10, P11, P12, P13, P14);
  and and_9 (and_9_out, G8, P9, P10, P11, P12, P13, P14);
  and and_10 (and_10_out, G9, P10, P11, P12, P13, P14);
  and and_11 (and_11_out, G10, P11, P12, P13, P14);
  and and_12 (and_12_out, G11, P12, P13, P14);
  and and_13 (and_13_out, G12, P13, P14);
  and and_14 (and_14_out, G13, P14);
  and and_15 (and_15_out, C, P0, P1, P2, P3, P4, P5, P6, P7, P8, P9, P10, P11, P12, P13, P14);
  or or_1 (C15, and_15_out, and_1_out, and_2_out, and_3_out, and_4_out, and_5_out, and_6_out, and_7_out, and_8_out, and_9_out, and_10_out, and_11_out, and_12_out, and_13_out, and_14_out, G14);
endmodule

module Carry16 (
  input  C,
  input  P0,
  input  P1,
  input  P2,
  input  P3,
  input  P4,
  input  P5,
  input  P6,
  input  P7,
  input  P8,
  input  P9,
  input  P10,
  input  P11,
  input  P12,
  input  P13,
  input  P14,
  input  P15,
  input  G0,
  input  G1,
  input  G2,
  input  G3,
  input  G4,
  input  G5,
  input  G6,
  input  G7,
  input  G8,
  input  G9,
  input  G10,
  input  G11,
  input  G12,
  input  G13,
  input  G14,
  input  G15,
  output C15
);

  wire and_1_out, and_2_out, and_3_out, and_4_out, and_5_out, and_6_out, and_7_out, and_8_out, and_9_out,
       and_10_out, and_11_out, and_12_out, and_13_out, and_14_out, and_15_out, and_16_out;

  and and_1 (and_1_out, G12, P13, P14, P15);
  and and_2 (and_2_out, G13, P14, P15);
  and and_3 (and_3_out, G14, P15);
  and and_4 (and_4_out, G0, P1, P2, P3, P4, P5, P6, P7, P8, P9, P10, P11, P12, P13, P14, P15);
  and and_5 (and_5_out, G1, P2, P3, P4, P5, P6, P7, P8, P9, P10, P11, P12, P13, P14, P15);
  and and_6 (and_6_out, G2, P3, P4, P5, P6, P7, P8, P9, P10, P11, P12, P13, P14, P15);
  and and_7 (and_7_out, G3, P4, P5, P6, P7, P8, P9, P10, P11, P12, P13, P14, P15);
  and and_8 (and_8_out, G4, P5, P6, P7, P8, P9, P10, P11, P12, P13, P14, P15);
  and and_9 (and_9_out, G5, P6, P7, P8, P9, P10, P11, P12, P13, P14, P15);
  and and_10 (and_10_out, G6, P7, P8, P9, P10, P11, P12, P13, P14, P15);
  and and_11 (and_11_out, G7, P8, P9, P10, P11, P12, P13, P14, P15);
  and and_12 (and_12_out, G8, P9, P10, P11, P12, P13, P14, P15);
  and and_13 (and_13_out, G9, P10, P11, P12, P13, P14, P15);
  and and_14 (and_14_out, G10, P11, P12, P13, P14, P15);
  and and_15 (and_15_out, G11, P12, P13, P14, P15);
  and and_16 (and_16_out, C, P0, P1, P2, P3, P4, P5, P6, P7, P8, P9, P10, P11, P12, P13, P14, P15);
  or or_1 (C15, and_16_out, and_4_out, and_5_out, and_6_out, and_7_out, and_8_out, and_9_out, and_10_out, and_11_out, and_12_out, and_13_out, and_14_out, and_15_out, and_1_out, and_2_out, and_3_out, G15);
endmodule

module Main (
  input  in_1,
  input  in_2,
  input  in_3,
  input  in_4,
  input  in_5,
  input  in_6,
  input  in_7,
  input  in_8,
  input  in_9,
  input  in_10,
  input  in_11,
  input  in_12
);

  wire n16bitadder_1_s1;

  _16BitAdder u_16bitadder_1 (
    .C(in_1), .A0(in_2), .B0(in_3), .A1(in_4), .B1(in_5), .A2(in_6), .B2(in_7), .S1(n16bitadder_1_s1));  // open: A3, B3, A4, B4, A5, B5, A6, B6, A7, B7, A8, B8, A9, B9, A10, B10, A11, B11, A12, B12, A13, B13, A14, B14, A15, B15, S0, S2, S3, S4, S5, S6, S7, S8, S9, S10, S11, S12, S13, S14, S15, C_2
  _7_Segment_Display u_7_segment_display_1 ();  // open: g, f, a, b, e, d, c, dp
  _7_Segment_Display u_7_segment_display_2 ();  // open: g, f, a, b, e, d, c, dp
  _7_Segment_Display u_7_segment_display_3 ();  // open: g, f, a, b, e, d, c, dp
  _7_Segment_Display u_7_segment_display_4 ();  // open: g, f, a, b, e, d, c, dp
  _7_Segment_Display u_7_segment_display_5 (.b(n16bitadder_1_s1), .c(n16bitadder_1_s1));  // open: g, f, a, e, d, dp
endmodule
